# Fritzing sketch Arduino_Tempalarm (saved by Fritzing 0.9.3b)

parts:
  Bauteil1 = Arduino Uno (Rev3)
  AMP1 = GF1002 Stereo Amplifier
  SP1 = SPEAKER [package=pcb_mount_speaker]
  RHT1 = Humidity and Temperature Sensor RHT03
  R1 = Resistor [tolerance=±5% resistance=220 package="0805 [SMD]"]  # not connected

nets:
  N1: Bauteil1.GND, AMP1.POWER-, RHT1.GND_2
  N2: Bauteil1.D2, RHT1.Data-signal
  N3: Bauteil1.D3_PWM, AMP1.INPUTL
  N4: AMP1.LOUT+, SP1.-
  N5: AMP1.LOUT-, SP1.+

notes:
  min. 7V
  5V über USB
  DHT11/22
  Verstärker

custom parts:
  GF1002 Stereo Amplifier: GF1002 6 Watt Stereo Amplifier
