# Fritzing sketch Arduino_Voltmeter (saved by Fritzing 0.9.3b)

parts:
  U1 = LuaNode32 / ESP32  # not connected
  AMP1 = GF1002 Stereo Amplifier
  SP1 = SPEAKER [package=pcb_mount_speaker]  # not connected
  U2 = ESP32S-HiLetgo [part_number=ESP32S-HiLetgo]  # not connected
  U3 = ESP32-38PinWide [part_number=ESP32-38PinWide]  # not connected

nets:
  N1: AMP1.ROUT+, AMP1.LOUT+

notes:
  Stromversorgung über USB
  Verstärker
  Meßspannung +
  0-3.3V -
  NodeMCU ESP8266 oder 32

custom parts:
  LuaNode32 / ESP32: ESP32 based LuaNode32
  GF1002 Stereo Amplifier: GF1002 6 Watt Stereo Amplifier
  ESP32S-HiLetgo: HiLetgo ESP-WROOM-32 ESP32 ESP-32S Development Board 2.4GHz Dual-Mode WiFi + Bluetooth Dual Cores Microcontroller The ESP32 integrated with Antenna switches, RF Balun, power amplifiers, low-noise amplifiers, filters, and management modules, and the entire solution occupies the least area of PCB. 2.4 GHz Wi-Fi plus Bluetooth dual-mode chip, with TSMC Ultra-low power consumption 40nm technology,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
  ESP32-38PinWide: Generic 38-Pin ESP32 with wide format (only access to one side of pins on a breadboard) based on Stephen Lilley's HiLetgo ESP-WROOM-32 ESP32 ESP-32S Development Board.
